# Fritzing sketch thumb_force_schematic (saved by Fritzing 0.7.7b)
breadboards: 1

parts:
  Arduino1 = Arduino
  LED1 = LED - 5mm [color="Green (565nm)" package="5 mm [THT]"]
  LED2 = LED - 5mm [color="Green (565nm)" package="5 mm [THT]"]
  LED3 = LED - 5mm [color="Yellow (595nm)" package="5 mm [THT]"]
  LED4 = LED - 5mm [color="Yellow (595nm)" package="5 mm [THT]"]
  LED5 = LED - 5mm [color="Red (660nm)" package="5 mm [THT]"]
  LED6 = LED - 5mm [color="Red (660nm)" package="5 mm [THT]"]
  J1 = Piezo Speaker
  J2 = Basic Servo
  R1 = Resistor [tolerance=±5% resistance=220 package=THT]
  J3 = Basic Force Sensing Resistor (FSR) [package=THT]

nets:
  GND: Arduino1.GND, LED1.cathode, LED2.cathode, LED3.cathode, LED4.cathode, LED5.cathode, LED6.cathode, J1.pin1, J2.gnd
  N1: Arduino1.D9, J1.pin2
  N2: Arduino1.D8, J2.pulse
  N3: Arduino1.D7, LED1.anode
  N4: Arduino1.D6, LED2.anode
  N5: Arduino1.D5, LED3.anode
  N6: Arduino1.D4, LED4.anode
  N7: Arduino1.D3, LED5.anode
  N8: Arduino1.D2, LED6.anode
  +5V: Arduino1.+5V, J2.vcc, R1.Pin_0, J3.pin_0
  N9: Arduino1.A0, R1.Pin_1, J3.pin_1

notes:
  Don't forget the voltage divider for the flex sensor!
